# Fritzing sketch Fan+SHT31_agrotech project (saved by Fritzing 0.9.3b)

parts:
  TP1 = TP4056 [chip_label=TP4056 package="DIP (Dual Inline) [THT]"]
  BATT1 = LiPoly Battery (1300mAh)
  M1 = FireBeetle ESP32-E
  A1 = 2 channel relay module [package=THT]
  JACK1 = 2.1mm Barrel Jack with Terminal Block  # not connected
  F1 = Fan - Ventilador [package=THT]
  F2 = Fan - Ventilador [package=THT]
  Part1 = Adafruit SHT31-D [part_number="Adafruit #2857"]
  Part2 = Solar Panel [package="Renogy 50 Watts 12 Volt Monocrystalline Bendable Solar Panel"]

nets:
  N1: TP1.pin1, Part2.Connector_1
  N2: TP1.pin2, Part2.Connector_2
  N3: TP1.pin3, M1.pin_12, M1.pin_20, A1.pin_14, Part1.GND
  N4: TP1.pin4, BATT1.negative
  N5: TP1.pin5, BATT1.positive
  N6: TP1.pin6, M1.pin_14, A1.pin_13
  N7: M1.pin_10, M1.pin_26, A1.pin_15, Part1.SDA
  N8: M1.pin_11, M1.pin_25, A1.pin_16, Part1.SCL
  N9: M1.pin_18, Part1.VCC
  N10: A1.pin_1, F1.5V
  GND: A1.pin_2, A1.pin_5, F1.GND, F2.GND
  N11: A1.pin_4, F2.5V

custom parts:
  TP4056: A DIP stand-in part for whatever IC you want. With 6 pins on a 300mil dual inline package (DIP) footprint.
  LiPoly Battery (1300mAh): Lithium Ion Polymer Battery (1300mAh)
  FireBeetle ESP32-E: FireBeetle ESP32-E, specially designed for IoT, is an ESP-WROOM-32E-based main controller board with dual-core chips. It supports WiFi and Bluetooth dual-mode communication and features a small size, ultra-low power consumption, on-board charging circuit, and easy-to-use interface, which can be conveniently used for smart home IoT, industrial IoT applications, wearable devices, and so on. You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
  2 channel relay module: 2 channel Relay Module 5V 12V 24V High and Low Level Trigger Relay Control With Optocoupler Two Way relays DC 5 V 12 V 24 V Volt.
  Fan - Ventilador: Ventilador de 2 pines, se encuentra comunmente en computadoras de escritorio
  Adafruit SHT31-D: Sensirion Temperature/Humidity sensors are some of the finest & highest-accuracy devices you can get. And, finally we have some that have a true I2C interface for easy reading. The SHT31-D sensor has an excellent ±2% relative humidity and ±0.3°C accuracy for most uses. We now use the version with a PTFE filter, it'll stay clean while still allowing humidity measurements to work Unlike earlier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
  Solar Panel: Renogy 50 Watts 12 Volt Solar Panel
