# Fritzing sketch arduino project (saved by Fritzing 0.9.3b)
breadboards: 1

parts:
  M1 = FireBeetle ESP32-E SMD
  U1 = Module 4 Relais 5V [package="Module 4 Relais 5V"]
  Capacitive_Soil_Moisture_Sensor1 = DFRobot Capacitive Soil Moisture Sensor V1.0 [part_number=SEN0193]
  Capacitive_Soil_Moisture_Sensor2 = DFRobot Capacitive Soil Moisture Sensor V1.0 [part_number=SEN0193]  # not connected
  Capacitive_Soil_Moisture_Sensor3 = DFRobot Capacitive Soil Moisture Sensor V1.0 [part_number=SEN0193]
  Part1 = Soil Moisture Sensor
  Part2 = Adafruit SHT31-D [part_number="Adafruit #2857"]
  VALVE1 = Plastic Solenoid Valve
  VALVE2 = Plastic Solenoid Valve
  VALVE4 = Plastic Solenoid Valve

nets:
  N1: M1.pin_9, Capacitive_Soil_Moisture_Sensor1.A
  N2: M1.pin_10, M1.pin_26, Part2.SDA
  N3: M1.pin_11, M1.pin_25, Part2.SCL
  GND: M1.pin_12, M1.pin_20, U1.GND, Capacitive_Soil_Moisture_Sensor3.GND, Part1.GND, Part2.GND
  VCC: M1.pin_14, U1.VCC, Capacitive_Soil_Moisture_Sensor3.VCC
  VCC_2: M1.pin_18, Part1.VCC, Part2.VCC
  N4: M1.pin_28, U1.IN4
  N5: M1.pin_29, U1.IN3
  N6: M1.pin_31, U1.IN2
  N7: M1.pin_32, U1.IN1
  N8: U1.K2-NF, VALVE1.no_name_yet#1, VALVE2.no_name_yet#1, VALVE4.no_name_yet#1
  N9: U1.K2-NO, VALVE4.no_name_yet#2
  N10: U1.K3-NO, VALVE2.no_name_yet#2
  N11: U1.K4-NO, VALVE1.no_name_yet#2

custom parts:
  FireBeetle ESP32-E SMD: FireBeetle ESP32-E, specially designed for IoT, is an ESP-WROOM-32E-based main controller board with dual-core chips. It supports WiFi and Bluetooth dual-mode communication and features a small size, ultra-low power consumption, on-board charging circuit, and easy-to-use interface, which can be conveniently used for smart home IoT, industrial IoT applications, wearable devices, and so on. You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
  Module 4 Relais 5V: Module 4 Relais 5V 4x SPD-06VDC-SD-C
  DFRobot Capacitive Soil Moisture Sensor V1.0: DFRobot Capacitive Soil Moisture Sensor V1.0 This product measures soil moisture levels by capacitive sensing, rather than resistive sensing like other types of moisture sensor. It is made of a corrosion resistant material giving it a long service life. Insert it into soil and impress your friends with the real-time soil moisture data! The product includes an on-board voltage regulator which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
  Adafruit SHT31-D: Sensirion Temperature/Humidity sensors are some of the finest & highest-accuracy devices you can get. And, finally we have some that have a true I2C interface for easy reading. The SHT31-D sensor has an excellent ±2% relative humidity and ±0.3°C accuracy for most uses. We now use the version with a PTFE filter, it'll stay clean while still allowing humidity measurements to work Unlike earlier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
